// Logisim project E8BC.circ as structural Verilog: 11 circuits, main circuit Mainboard
module ALU (
  input  [7:0] A,
  input  [1:0] FN,
  input  [7:0] B,
  input  SUB,
  input  WC,
  input  CF,
  input  [1:0] REG,
  output [7:0] OUT,
  output CY_OUT
);

  wire multiplexer_2_out;
  wire [7:0] ADD_SUB_out_6, AND_out_3, multiplexer_1_out, OR_out_3, XOR_out_3;

  Multiplexer #(.select(2), .width(8), .enable("false")) multiplexer_1 (
    .in0(B), .in1({8{1'b0}}), .in2(8'h1), .in3({8{1'b0}}), .out(multiplexer_1_out), .sel(REG));
  Multiplexer #(.enable("false")) multiplexer_2 (.in0(1'b0), .in1(CF), .out(multiplexer_2_out), .sel(WC));
  AND8b AND (.in_1(A), .in_2(multiplexer_1_out), .out_3(AND_out_3));
  OR8b OR (.in_1(A), .in_2(multiplexer_1_out), .out_3(OR_out_3));
  XOR8b XOR (.in_1(A), .in_2(multiplexer_1_out), .out_3(XOR_out_3));
  ADD_SUB_CY ADD_SUB (
    .A(A), .in_2(multiplexer_1_out), .CIN(multiplexer_2_out), .SUB(SUB), .COUT(CY_OUT), .out_6(ADD_SUB_out_6));
  Multiplexer #(.select(2), .width(8), .enable("false")) multiplexer_3 (
    .in0(AND_out_3), .in1(OR_out_3), .in2(XOR_out_3), .in3(ADD_SUB_out_6), .out(OUT), .sel(FN));

  // Notes on the sheet:
  //   WC: pull=up
  //   REG: pull=up
  //   CY_OUT: pull=up
  //   CF: pull=up
  //   A: pull=up
  //   OUT: pull=up
  //   B: pull=up
  //   SUB: pull=up
  //   FN: pull=up
endmodule

module AND8b (
  input  [7:0] in_1,
  input  [7:0] in_2,
  output [7:0] out_3
);

  and and_1 (out_3[0], in_1[0], in_2[0]);
  and and_2 (out_3[1], in_1[1], in_2[1]);
  and and_3 (out_3[2], in_1[2], in_2[2]);
  and and_4 (out_3[3], in_1[3], in_2[3]);
  and and_5 (out_3[4], in_1[4], in_2[4]);
  and and_6 (out_3[5], in_1[5], in_2[5]);
  and and_7 (out_3[6], in_1[6], in_2[6]);
  and and_8 (out_3[7], in_1[7], in_2[7]);

  // Notes on the sheet:
  //   in_1: pull=up
  //   out_3: pull=up
  //   in_2: pull=up
endmodule

module OR8b (
  input  [7:0] in_1,
  input  [7:0] in_2,
  output [7:0] out_3
);

  or or_1 (out_3[0], in_1[0], in_2[0]);
  or or_2 (out_3[1], in_1[1], in_2[1]);
  or or_3 (out_3[2], in_1[2], in_2[2]);
  or or_4 (out_3[3], in_1[3], in_2[3]);
  or or_5 (out_3[4], in_1[4], in_2[4]);
  or or_6 (out_3[5], in_1[5], in_2[5]);
  or or_7 (out_3[6], in_1[6], in_2[6]);
  or or_8 (out_3[7], in_1[7], in_2[7]);

  // Notes on the sheet:
  //   in_2: pull=up
  //   out_3: pull=up
  //   in_1: pull=up
endmodule

module XOR8b (
  input  [7:0] in_1,
  input  [7:0] in_2,
  output [7:0] out_3
);

  xor xor_1 (out_3[0], in_1[0], in_2[0]);
  xor xor_2 (out_3[1], in_1[1], in_2[1]);
  xor xor_3 (out_3[2], in_1[2], in_2[2]);
  xor xor_4 (out_3[3], in_1[3], in_2[3]);
  xor xor_5 (out_3[4], in_1[4], in_2[4]);
  xor xor_6 (out_3[5], in_1[5], in_2[5]);
  xor xor_7 (out_3[6], in_1[6], in_2[6]);
  xor xor_8 (out_3[7], in_1[7], in_2[7]);

  // Notes on the sheet:
  //   in_2: pull=up
  //   out_3: pull=up
  //   in_1: pull=up
endmodule

module ADD_SUB_CY (
  input  [7:0] A,
  input  [7:0] in_2,
  input  CIN,
  input  SUB,
  output COUT,
  output [7:0] out_6
);

  wire adder_1_cout, subtractor_1_bout;
  wire [7:0] adder_1_out, subtractor_1_out;

  Adder adder_1 (.a(A), .b(in_2), .out(adder_1_out), .cin(CIN), .cout(adder_1_cout));
  Subtractor subtractor_1 (.a(A), .b(in_2), .out(subtractor_1_out), .bin(CIN), .bout(subtractor_1_bout));
  Multiplexer #(.enable("false")) multiplexer_1 (.in0(adder_1_cout), .in1(subtractor_1_bout), .out(COUT), .sel(SUB));
  Multiplexer #(.width(8), .enable("false")) multiplexer_2 (
    .in0(adder_1_out), .in1(subtractor_1_out), .out(out_6), .sel(SUB));

  // Notes on the sheet:
  //   CIN: pull=up
  //   in_2: pull=up
  //   out_6: pull=up
  //   COUT: pull=up
  //   A: pull=up
  //   SUB: pull=up
endmodule

module Flag (
  input  [7:0] ALU_OUT,
  input  ALU_CY,
  input  CLK,
  input  CLRF,
  output [7:0] out_5
);

  wire or_1_out;
  wire [0:0] not_1_out;

  or or_1 (or_1_out, ALU_OUT[0], ALU_OUT[1], ALU_OUT[2], ALU_OUT[3], ALU_OUT[4], ALU_OUT[5], ALU_OUT[6], ALU_OUT[7]);
  Register FLAG (.D({{6{1'b0}}, ALU_CY, not_1_out[0]}), .en(1'b1), .Q(out_5), .clk(CLK), .clr(CLRF));
  not not_1 (not_1_out[0], or_1_out);

  // Notes on the sheet:
  //   CLRF: pull=up
  //   CLK: pull=up
  //   ALU_OUT: pull=up
  //   out_5: pull=up
  //   ALU_CY: pull=up
endmodule

module Controller (
  input  [7:0] IR,
  input  CLK,
  input  ZF,
  input  CLR,
  output WC,
  output [1:0] ALU_REG,
  output [1:0] ALU_FUN,
  output ALU_SUB,
  output ALU_RD,
  output A_WR,
  output A_RD,
  output B_WR,
  output B_RD,
  output COUNT_INC,
  output IR_WR,
  output LO_WR,
  output HI_WR,
  output RAM_WR,
  output RAM_RD,
  output ROM_RD,
  output LD_COUNT,
  output IO1_RD,
  output IO2_RD,
  output IO3_WR,
  output IO4_WR,
  output HLT
);

  wire multiplexer_1_out, not_1_out, or_1_out, Ring_Counter_t1, Ring_Counter_t4;
  wire [7:0] counter_1_q;
  wire [31:11] rom_1_data;

  Multiplexer #(.enable("false")) multiplexer_1 (
    .in0(1'b1), .in1(1'b0), .out(multiplexer_1_out), .sel(Ring_Counter_t4));
  Counter counter_1 (
    .load(Ring_Counter_t4), .D(IR), .count(multiplexer_1_out), .Q(counter_1_q), .clk(not_1_out),
    .clr(Ring_Counter_t1));  // open: carry
  ROM #(.dataWidth(32)) rom_1 (
    .addr(counter_1_q),
    .data({rom_1_data[31], HLT, rom_1_data[29:25], IO4_WR, IO3_WR, IO2_RD, rom_1_data[21], IO1_RD, LD_COUNT, ROM_RD, RAM_RD, RAM_WR, HI_WR, LO_WR, IR_WR, COUNT_INC, rom_1_data[11], B_RD, B_WR, A_RD, A_WR, ALU_RD, ALU_SUB, ALU_FUN, ALU_REG, WC}),
    .sel(1'b1));
  or or_1 (or_1_out, rom_1_data[31], CLR);
  not not_1 (not_1_out, CLK);
  Shift_counter Ring_Counter (.CLK(CLK), .CLR(or_1_out), .T1(Ring_Counter_t1), .T4(Ring_Counter_t4));  // open: T2, T3

  // Notes on the sheet:
  //   contents of rom_1 (hex, n*v repeats v):
  //   42000 1000 4*0 40200 1000 80000000 7*0 10100 80000000 44*0 40080 1000 80000000 80000000 37*0 8100
  //   80000000 6*0 4100 80000000 5*0 40000000 0 480 80000000 6*0 d8 80000000 6*0 d9 80000000 73*0 800100
  //   80000000
endmodule

module Shift_counter (
  input  CLK,
  input  CLR,
  output T1,
  output T2,
  output T3,
  output T4
);

  wire d_ff_4_qn, d_ff_5_q;

  D_Flip_Flop d_ff_1 (.clk(CLK), .D(d_ff_5_q), .Q(T1), .preset(CLR), .en(1'b1));  // open: Qn, reset
  D_Flip_Flop d_ff_2 (.clk(CLK), .D(T1), .Q(T2), .en(1'b1), .reset(CLR));  // open: Qn, preset
  D_Flip_Flop d_ff_3 (.clk(CLK), .D(T2), .Q(T3), .en(1'b1), .reset(CLR));  // open: Qn, preset
  D_Flip_Flop d_ff_4 (.clk(CLK), .D(T3), .Q(T4), .Qn(d_ff_4_qn), .en(1'b1), .reset(CLR));  // open: preset
  D_Flip_Flop d_ff_5 (.D(T4), .Q(d_ff_5_q), .reset(CLR));  // open: clk, Qn, preset, en
endmodule

module Mainboard (
  input  RESET,
  input  MAN_CLK,
  input  MAN_AUTO,
  input  HALT
);

  wire CLOCK_out, microprocessor_1_hlt, microprocessor_1_ram_rd, microprocessor_1_ram_wr,
       microprocessor_1_rom_rd, multiplexer_1_out, multiplexer_2_out, or_1_out;
  wire [7:0] controlled_buffer_1_out, controlled_buffer_3_out, microprocessor_1_io3,
       microprocessor_1_mem_out, ram_1_data, rom_1_data;
  wire [15:0] microprocessor_1_adr_ram, microprocessor_1_adr_rom;

  Multiplexer #(.enable("false")) multiplexer_1 (
    .in0(MAN_CLK), .in1(CLOCK_out), .out(multiplexer_1_out), .sel(MAN_AUTO));
  Clock CLOCK (.out(CLOCK_out));
  RAM #(.addrWidth(16), .bus("separate")) ram_1 (
    .addr(microprocessor_1_adr_ram), .din(controlled_buffer_3_out), .data(ram_1_data),
    .str(microprocessor_1_ram_wr), .sel(1'b1), .clk(multiplexer_2_out), .ld(microprocessor_1_ram_rd));  // open: clr
  ROM #(.addrWidth(16)) rom_1 (.addr(microprocessor_1_adr_rom), .data(rom_1_data), .sel(1'b1));
  assign controlled_buffer_1_out = microprocessor_1_ram_rd ? ram_1_data : 8'bz;  // Controlled_Buffer controlled_buffer_1
  assign controlled_buffer_1_out = microprocessor_1_rom_rd ? rom_1_data : 8'bz;  // Controlled_Buffer controlled_buffer_2
  Multiplexer #(.enable("false")) multiplexer_2 (
    .in0(multiplexer_1_out), .in1(1'b0), .out(multiplexer_2_out), .sel(or_1_out));
  or or_1 (or_1_out, microprocessor_1_hlt, HALT);
  assign controlled_buffer_3_out = microprocessor_1_ram_wr ? microprocessor_1_mem_out : 8'bz;  // Controlled_Buffer controlled_buffer_3
  Microprocessor microprocessor_1 (
    .CLK(multiplexer_2_out), .CLR(RESET), .ADR_RAM(microprocessor_1_adr_ram),
    .RAM_WR(microprocessor_1_ram_wr), .RAM_RD(microprocessor_1_ram_rd), .ROM_RD(microprocessor_1_rom_rd),
    .ADR_ROM(microprocessor_1_adr_rom), .IO3(microprocessor_1_io3), .MEM_OUT(microprocessor_1_mem_out),
    .MEM_IN(controlled_buffer_1_out), .HLT(microprocessor_1_hlt));  // open: IO1, IO2, IO4
  LED led_1 (.in(microprocessor_1_io3[7]));
  LED led_2 (.in(microprocessor_1_io3[5]));
  LED led_3 (.in(microprocessor_1_io3[6]));
  LED led_4 ();  // open: in
  TTY tty_1 (.clk(multiplexer_2_out), .clr(RESET));  // open: data, we
  Keyboard keyboard_1 (.clk(multiplexer_2_out), .re(1'b1));  // open: clr, avail, data
  LED led_5 (.in(microprocessor_1_io3[3]));
  LED led_6 (.in(microprocessor_1_io3[4]));
  LED led_7 ();  // open: in
  LED led_8 ();  // open: in
  LED led_9 ();  // open: in
  LED led_10 ();  // open: in
  LED led_11 (.in(microprocessor_1_io3[0]));
  LED led_12 (.in(microprocessor_1_io3[2]));
  LED led_13 (.in(microprocessor_1_io3[1]));
  LED led_14 ();  // open: in
  LED led_15 ();  // open: in
  LED led_16 ();  // open: in

  // Notes on the sheet:
  //   contents of rom_1 (hex, n*v repeats v):
  //   3e aa 67 3e 1 6f 3e ff 10 76
endmodule

module test (
  input  [7:0] in_1,
  output [7:0] out_2
);

  ROM rom_1 (.addr(in_1), .data(out_2), .sel(1'b1));

  // Notes on the sheet:
  //   contents of rom_1 (hex, n*v repeats v):
  //   aa bb cc dd
endmodule

module Microprocessor (
  input  [7:0] MEM_IN,
  input  CLK,
  input  [7:0] IO1,
  input  CLR,
  input  [7:0] IO2,
  output [15:0] ADR_RAM,
  output [7:0] MEM_OUT,
  output RAM_WR,
  output RAM_RD,
  output ROM_RD,
  output [15:0] ADR_ROM,
  output HLT,
  output [7:0] IO3,
  output [7:0] IO4
);

  wire ALU_cy_out, CF, Controller_a_rd, Controller_a_wr, Controller_alu_rd, Controller_alu_sub,
       Controller_b_rd, Controller_b_wr, Controller_wc, COUNT_INC, HI_WR, IO1_RD, IO2_RD, IO3_WR, IO4_WR,
       IR_WR, LD_COUNT, LO_WR, not_1_out, or_1_out, ZF;
  wire [1:0] Controller_alu_fun, Controller_alu_reg;
  wire [7:0] A_q, ALU_out, B_q, IR, PORT1_q, PORT2_q;

  Register LO (.D(MEM_IN), .en(LO_WR), .Q(ADR_RAM[7:0]), .clk(CLK), .clr(CLR));
  Register HI (.D(MEM_IN), .en(HI_WR), .Q(ADR_RAM[15:8]), .clk(CLK), .clr(CLR));
  Counter #(.width(16), .max('hffff)) COUNTER (
    .load(LD_COUNT), .D(ADR_RAM), .count(COUNT_INC), .Q(ADR_ROM), .clk(CLK), .clr(CLR));  // open: carry
  Register u_IR (.D(MEM_IN), .en(IR_WR), .Q(IR), .clk(CLK), .clr(CLR));
  Register PORT1 (.D(IO1), .en(1'b1), .Q(PORT1_q), .clk(CLK), .clr(CLR));
  Register PORT2 (.D(IO2), .en(1'b1), .Q(PORT2_q), .clk(CLK), .clr(CLR));
  assign MEM_IN = IO1_RD ? PORT1_q : 8'bz;  // Controlled_Buffer controlled_buffer_1
  assign MEM_IN = IO2_RD ? PORT2_q : 8'bz;  // Controlled_Buffer controlled_buffer_2
  assign MEM_IN = Controller_alu_rd ? ALU_out : 8'bz;  // Controlled_Buffer controlled_buffer_3
  assign MEM_IN = Controller_a_rd ? A_q : 8'bz;  // Controlled_Buffer controlled_buffer_4
  assign MEM_IN = Controller_b_rd ? B_q : 8'bz;  // Controlled_Buffer controlled_buffer_5
  Register A (.D(MEM_IN), .en(Controller_a_wr), .Q(A_q), .clk(CLK), .clr(CLR));
  Register B (.D(MEM_IN), .en(Controller_b_wr), .Q(B_q), .clk(CLK), .clr(CLR));
  Register PORT3 (.D(MEM_IN), .en(IO3_WR), .Q(IO3), .clk(CLK), .clr(CLR));
  Register PORT4 (.D(MEM_IN), .en(IO4_WR), .Q(IO4), .clk(CLK), .clr(CLR));
  ALU ALU (
    .A(A_q), .B(B_q), .WC(Controller_wc), .OUT(ALU_out), .CF(CF), .REG(Controller_alu_reg),
    .SUB(Controller_alu_sub), .FN(Controller_alu_fun), .CY_OUT(ALU_cy_out));
  or or_1 (or_1_out, ALU_out[0], ALU_out[1], ALU_out[2], ALU_out[3], ALU_out[4], ALU_out[5], ALU_out[6], ALU_out[7]);
  Controller Controller (
    .WC(Controller_wc), .ALU_REG(Controller_alu_reg), .ALU_FUN(Controller_alu_fun), .IR(IR),
    .ALU_SUB(Controller_alu_sub), .ALU_RD(Controller_alu_rd), .A_WR(Controller_a_wr), .A_RD(Controller_a_rd),
    .B_WR(Controller_b_wr), .B_RD(Controller_b_rd), .COUNT_INC(COUNT_INC), .IR_WR(IR_WR), .LO_WR(LO_WR),
    .HI_WR(HI_WR), .RAM_WR(RAM_WR), .RAM_RD(RAM_RD), .ROM_RD(ROM_RD), .LD_COUNT(LD_COUNT), .IO1_RD(IO1_RD),
    .IO2_RD(IO2_RD), .IO3_WR(IO3_WR), .IO4_WR(IO4_WR), .CLR(CLR), .CLK(CLK), .ZF(ZF), .HLT(HLT));
  not not_1 (not_1_out, or_1_out);
  Register #(.width(1)) u_ZF (.D(not_1_out), .en(1'b1), .Q(ZF), .clk(CLK), .clr(CLR));
  Register #(.width(1)) u_CF (.D(ALU_cy_out), .en(1'b1), .Q(CF), .clk(CLK), .clr(CLR));

  assign MEM_OUT = MEM_IN;
endmodule
